# Fritzing sketch FKJNGRWI7W1SKB9 (saved by Fritzing 0.9.3b)
breadboards: 1

parts:
  Part1 = Arduino Uno (Rev3)
  LCD1 = LCD screen
  Part2 = Real Time Clock Module - DS1307 RTC Breakout Board
  R1_220_Ohm = Resistor [tolerance=±5% resistance=220 package="0805 [SMD]"]
  S1 = Pushbutton [package="[THT]"]
  R1_220_Ohm_2 = Resistor [tolerance=±5% resistance=220 package="0805 [SMD]"]
  Rotary_Encoder_KY-040_(wires_are_labelled) = ENCODER_2LED [package=encoder_led_2]
  C1_0_47uf = Electrolytic Capacitor [capacitance=1000μF package="1010 [SMD, electrolytic]"]
  C1_0_47uf_1 = Electrolytic Capacitor [capacitance=1000μF package="1010 [SMD, electrolytic]"]
  R2_10K = Resistor [tolerance=±5% resistance=220 package="0805 [SMD]"]
  J1_Stir_Servo_(Signal_to_10) = Basic Servo
  J2_Continuous_Auger_Servo_(Signal_to_9) = Basic Servo
  R2_2_2k = Resistor [tolerance=±5% resistance=220 package="2512 [SMD]"]

nets:
  N1: Part1.A3, S1.Pin_3, S1.Pin_4, R1_220_Ohm_2.Pin_1
  N2: Part1.A4/SDA, Part2.SDA
  N3: Part1.A5/SCL, Part2.SCL
  N4: Part1.D8, LCD1.DB5
  N5: Part1.D9_PWM, J2_Continuous_Auger_Servo_(Signal_to_9).pulse
  N6: Part1.D10_PWM/SS, J1_Stir_Servo_(Signal_to_10).pulse
  N7: Part1.D11_PWM/MOSI, LCD1.E
  N8: Part1.D12/MISO, LCD1.RS
  N9: Part1.D2, Rotary_Encoder_KY-040_(wires_are_labelled).B, C1_0_47uf.+
  N10: Part1.D3_PWM, Rotary_Encoder_KY-040_(wires_are_labelled).C, C1_0_47uf_1.+
  N11: Part1.D4, Rotary_Encoder_KY-040_(wires_are_labelled).-, R2_10K.Pin_0
  N12: Part1.D5_PWM, LCD1.DB4
  N13: Part1.D6_PWM, LCD1.DB7
  N14: Part1.D7, LCD1.DB6
  5V: Part1.5V, LCD1.VDD, Part2.5V, R1_220_Ohm.Pin_0, S1.Pin_1, S1.Pin_2, Rotary_Encoder_KY-040_(wires_are_labelled).+G, R2_10K.Pin_1, J1_Stir_Servo_(Signal_to_10).vcc, J2_Continuous_Auger_Servo_(Signal_to_9).vcc
  GND: Part1.GND, LCD1.VSS, LCD1.R/W, LCD1.LED-, Part2.GND, R1_220_Ohm_2.Pin_0, Rotary_Encoder_KY-040_(wires_are_labelled).SW, C1_0_47uf.-, C1_0_47uf_1.-, J1_Stir_Servo_(Signal_to_10).gnd, R2_2_2k.Pin_0
  N15: LCD1.V0, R2_2_2k.Pin_1
  N16: LCD1.LED+, R1_220_Ohm.Pin_1
